# Fritzing sketch wifi-therm (saved by Fritzing 0.9.4)
circuit board: 8.46667cm x 5.64444cm

parts:
  MH-ET_Live_Minikit_for_ESP1 = MH-ET Live Minikit for ESP32
  LED1 = LED - 5mm [color="Red (633nm)" package="5 mm [THT]"]
  R2 = Resistor [tolerance=±5% resistance=220 package=THT]
  DS1 = DS18B20 1-Wire Temperature Sensor [part_number=DS18B20]
  R3 = Resistor [tolerance=±5% resistance=4.7k package=THT]

nets:
  GND: MH-ET_Live_Minikit_for_ESP1.GND, LED1.cathode, DS1.GND
  N1: MH-ET_Live_Minikit_for_ESP1.TMS, R2.Pin_0
  N2: MH-ET_Live_Minikit_for_ESP1.IO18, DS1.DQ, R3.Pin_1
  3.3V: MH-ET_Live_Minikit_for_ESP1.3.3V, DS1.VDD, R3.Pin_0
  N3: LED1.anode, R2.Pin_1

custom parts:
  MH-ET Live Minikit for ESP32: MH-ET Live Minikit for ESP32 ( http://mh.nodebb.com/topic/8/mh-et-live-minikit-for-esp32/2/) PCB footprint is invalid.
